// Logisim project p1.circ as structural Verilog: 1 circuit, main circuit main
module main (
  input  x,
  input  y,
  input  x_2,
  input  y_2,
  input  x_3,
  input  x_4,
  input  y_3,
  input  in_8,
  input  in_9,
  output x_y,
  output x_y_2,
  output x_prime,
  output x_y_3,
  output out_14
);

  or or_1 (x_y, x, y);
  and and_1 (x_y_2, x_2, y_2);
  not not_1 (x_prime, x_3);
  xor xor_1 (x_y_3, x_4, y_3);
  xnor xnor_1 (out_14, in_8, in_9);

  // Notes on the sheet:
  //   or gate
  //   and gate
  //   not gate
  //   xor gate
  //   xnor gate
endmodule
