// Logisim project p15.circ as structural Verilog: 1 circuit, main circuit main
module main (
  input  j,
  input  k,
  input  d,
  input  t,
  output q,
  output q_prime,
  output q_2,
  output q_prime_2,
  output q_3,
  output q_prime_3
);

  wire clock_1_out, clock_2_out, clock_3_out;

  Clock clock_1 (.out(clock_1_out));
  Clock clock_2 (.out(clock_2_out));
  Clock clock_3 (.out(clock_3_out));
  J_K_Flip_Flop j_k_ff_1 (.J(j), .clk(clock_1_out), .K(k), .Q(q), .Qn(q_prime));  // open: preset, en, reset
  D_Flip_Flop d_ff_1 (.clk(clock_2_out), .D(d), .Q(q_2), .Qn(q_prime_2));  // open: preset, en, reset
  T_Flip_Flop t_ff_1 (.clk(clock_3_out), .T(t), .Q(q_3), .Qn(q_prime_3));  // open: preset, reset, en

  // Notes on the sheet:
  //   clk
  //   clk
  //   clk
  //   jk-flipflop
  //   d-flipflop
  //   t-flipflop
endmodule
