// Logisim project p16.circ as structural Verilog: 1 circuit, main circuit main
module main (
  input  in_1,
  input  in_2,
  input  in_3,
  input  in_4,
  input  in_5,
  input  in_6,
  output out_7
);

  wire button_1_out, button_2_out, button_3_out, clock_1_out, clock_2_out, clock_3_out, d_ff_1_q, d_ff_2_q,
       d_ff_3_q, d_ff_4_q, d_ff_5_q, d_ff_6_q, d_ff_7_q, d_ff_8_q, d_ff_9_q, d_ff_10_q, d_ff_12_q, undriven,
       undriven_2, undriven_3, undriven_4;

  Clock clock_1 (.out(clock_1_out));
  Button button_1 (.out(button_1_out));
  Clock clock_2 (.out(clock_2_out));
  Clock clock_3 (.out(clock_3_out));
  Button button_2 (.out(button_2_out));
  Button button_3 (.out(button_3_out));
  D_Flip_Flop d_ff_1 (.clk(clock_1_out), .D(in_1), .Q(d_ff_1_q), .reset(button_1_out));  // open: Qn, preset, en
  D_Flip_Flop d_ff_2 (.D(in_2), .Q(d_ff_2_q), .reset(button_3_out));  // open: clk, Qn, preset, en
  D_Flip_Flop d_ff_3 (.clk(clock_3_out), .D(undriven), .Q(d_ff_3_q), .reset(button_2_out));  // open: Qn, preset, en
  LED led_1 (.in(d_ff_3_q));
  D_Flip_Flop d_ff_4 (.clk(clock_1_out), .D(d_ff_1_q), .Q(d_ff_4_q), .reset(button_1_out));  // open: Qn, preset, en
  LED led_2 (.in(d_ff_2_q));
  D_Flip_Flop d_ff_5 (.clk(clock_3_out), .D(undriven_2), .Q(d_ff_5_q), .reset(button_2_out));  // open: Qn, preset, en
  LED led_3 (.in(d_ff_5_q));
  D_Flip_Flop d_ff_6 (.clk(clock_1_out), .D(d_ff_4_q), .Q(d_ff_6_q), .reset(button_1_out));  // open: Qn, preset, en
  LED led_4 (.in(d_ff_7_q));
  D_Flip_Flop d_ff_7 (.D(d_ff_2_q), .Q(d_ff_7_q), .reset(button_3_out));  // open: clk, Qn, preset, en
  D_Flip_Flop d_ff_8 (.D(d_ff_7_q), .Q(d_ff_8_q), .reset(button_3_out));  // open: clk, Qn, preset, en
  D_Flip_Flop d_ff_9 (.clk(clock_3_out), .D(undriven_3), .Q(d_ff_9_q), .reset(button_2_out));  // open: Qn, preset, en
  LED led_5 (.in(d_ff_9_q));
  D_Flip_Flop d_ff_10 (.clk(clock_1_out), .D(d_ff_6_q), .Q(d_ff_10_q), .reset(button_1_out));  // open: Qn, preset, en
  LED led_6 (.in(d_ff_10_q));
  LED led_7 (.in(d_ff_8_q));
  D_Flip_Flop d_ff_11 (.clk(clock_2_out), .D(d_ff_8_q), .Q(out_7), .reset(button_3_out));  // open: Qn, preset, en
  D_Flip_Flop d_ff_12 (.clk(clock_3_out), .D(undriven_4), .Q(d_ff_12_q), .reset(button_2_out));  // open: Qn, preset, en
  LED led_8 (.in(d_ff_12_q));
  LED led_9 (.in(out_7));

  // Notes on the sheet:
  //   siso
  //   sipo
  //   pipo
endmodule
