// Logisim project p19.circ as structural Verilog: 1 circuit, main circuit main
module main (
  input  a,
  input  b,
  input  c_in,
  input  [1:0] operation,
  output result,
  output out_6
);

  wire adder_1_out, and_1_out, or_1_out;

  or or_1 (or_1_out, a, b);
  and and_1 (and_1_out, a, b);
  Adder #(.width(1)) adder_1 (.a(a), .b(b), .out(adder_1_out), .cin(c_in), .cout(out_6));
  Multiplexer #(.select(2)) multiplexer_1 (
    .in0(or_1_out), .in1(and_1_out), .in2(adder_1_out), .out(result), .sel(operation));  // open: in3, en

  // Notes on the sheet:
  //   c-out
endmodule
