// Logisim project p20.circ as structural Verilog: 1 circuit, main circuit main
module main (
  input  a0,
  input  b0,
  input  a1,
  input  b1,
  input  a2,
  input  b2,
  input  a3,
  input  b3,
  output s0,
  output s1,
  output s2,
  output s3,
  output s4
);

  wire adder_1_cout, adder_2_cout, adder_3_cout;

  Adder #(.width(1)) adder_1 (.a(a0), .b(b0), .out(s0), .cout(adder_1_cout));  // open: cin
  Adder #(.width(1)) adder_2 (.a(a1), .b(b1), .out(s1), .cin(adder_1_cout), .cout(adder_2_cout));
  Adder #(.width(1)) adder_3 (.a(a2), .b(b2), .out(s2), .cin(adder_2_cout), .cout(adder_3_cout));
  Adder #(.width(1)) adder_4 (.a(a3), .b(b3), .out(s3), .cin(adder_3_cout), .cout(s4));
endmodule
