// Logisim project p3.circ as structural Verilog: 1 circuit, main circuit main
module main (
  input  x,
  input  y,
  input  x_2,
  input  y_2,
  input  x_3,
  output x_y,
  output out_7,
  output out_8
);

  wire nor_1_out, nor_2_out, nor_3_out;

  nor nor_1 (nor_1_out, x, y);
  nor nor_2 (nor_2_out, x_2, x_2);
  nor nor_3 (nor_3_out, y_2, y_2);
  nor nor_4 (x_y, nor_1_out, nor_1_out);
  nor nor_5 (out_7, nor_2_out, nor_3_out);
  nor nor_6 (out_8, x_3, x_3);

  // Notes on the sheet:
  //   ('x."y)
  //   'x.'y
  //   'x.'y
  //   'x
  //   'y
  //   x.y
  //   'x
endmodule
