// Logisim project p9.circ as structural Verilog: 1 circuit, main circuit main
module main (
  input  a,
  input  b,
  output difference,
  output borrow
);

  wire not_1_out;

  xor xor_1 (difference, a, b);
  not not_1 (not_1_out, a);
  and and_1 (borrow, not_1_out, b);
endmodule
